# Fritzing sketch parallel_resistor (saved by Fritzing 0.9.0b)
breadboards: 1

parts:
  Bauteil1 = Arduino Uno (Rev3)
  R1 = Resistor [tolerance=±5% resistance=100 package=THT]
  R2 = Resistor [tolerance=±5% resistance=100 package=THT]

nets:
  N1: Bauteil1.A0, Bauteil1.5V, R1.Pin_0, R2.Pin_0
  N2: Bauteil1.GND, R1.Pin_1, R2.Pin_1
